// Logisim project ALU.circ as structural Verilog: 1 circuit, main circuit main
module main (
  input  [15:0] A,
  input  [15:0] B,
  input  clk,
  input  [5:0] ALUOpcode,
  output [15:0] R
);

  wire [0:0] comparator_1_eq, comparator_1_lt, demultiplexer_1_out2, demultiplexer_1_out8, or_4_out;
  wire [14:0] demultiplexer_1_out2_2, demultiplexer_1_out8_2, or_4_out_2;
  wire [15:0] Add_s, AddI_s, and_1_out, and_2_out, and_3_out, and_4_out, and_5_out, and_6_out, and_7_out,
       and_8_out, and_9_out, and_10_out, and_11_out, demultiplexer_1_out0, demultiplexer_1_out1,
       demultiplexer_1_out3, demultiplexer_1_out4, demultiplexer_1_out5, demultiplexer_1_out6,
       demultiplexer_1_out7, demultiplexer_1_out9, demultiplexer_1_out10, demultiplexer_1_out11,
       demultiplexer_1_out12, demultiplexer_1_out13, demultiplexer_1_out15, divider_1_out, main_1_hi,
       main_1_lo, multiplexer_1_out, or_1_out, or_2_out, or_3_out, shifter_1_out, subtractor_1_out;

  ALUAdder_main Add (.A(A), .C_in(1'b0), .B(B), .S(Add_s));  // open: C_out
  Subtractor #(.width(16)) subtractor_1 (.a(A), .b(B), .out(subtractor_1_out), .bin(1'b0));  // open: bout
  ALUAdder_main AddI (.A(A), .C_in(1'b0), .B(B), .S(AddI_s));  // open: C_out
  Shifter #(.width(16)) shifter_1 (.in(A), .\dist (B[3:0]), .out(shifter_1_out));
  Comparator #(.width(16)) comparator_1 (.a(A), .b(B), .eq(comparator_1_eq[0]), .lt(comparator_1_lt[0]));  // open: gt
  Divider #(.width(16)) divider_1 (.a(A), .b(B), .out(divider_1_out));  // open: upper, rem
  Demultiplexer #(.select(4), .width(16), .disabled(0)) demultiplexer_1 (
    .out0(demultiplexer_1_out0), .out1(demultiplexer_1_out1),
    .out2({demultiplexer_1_out2_2, demultiplexer_1_out2[0]}), .out3(demultiplexer_1_out3),
    .out4(demultiplexer_1_out4), .out5(demultiplexer_1_out5), .out6(demultiplexer_1_out6),
    .out7(demultiplexer_1_out7), .out8({demultiplexer_1_out8_2, demultiplexer_1_out8[0]}),
    .out9(demultiplexer_1_out9), .out10(demultiplexer_1_out10), .out11(demultiplexer_1_out11),
    .out12(demultiplexer_1_out12), .out13(demultiplexer_1_out13), .out15(demultiplexer_1_out15),
    .in({16{1'b1}}), .sel(ALUOpcode[3:0]), .en(clk));  // open: out14
  ALUMult_main main_1 (.A(A), .B(B), .lo(main_1_lo), .hi(main_1_hi), .write(demultiplexer_1_out2[0]), .clk(clk));
  assign and_1_out = A & B;  // AND_Gate and_1, 16 bits wide
  assign or_1_out = A | B;  // OR_Gate or_1, 16 bits wide
  assign or_2_out = demultiplexer_1_out10 | demultiplexer_1_out11 | demultiplexer_1_out0;  // OR_Gate or_2, 16 bits wide
  assign or_3_out = {{15{1'b0}}, comparator_1_eq[0]} | {{15{1'b0}}, comparator_1_lt[0]};  // OR_Gate or_3, 16 bits wide
  assign and_2_out = Add_s & or_2_out;  // AND_Gate and_2, 16 bits wide
  assign and_3_out = subtractor_1_out & demultiplexer_1_out1;  // AND_Gate and_3, 16 bits wide
  assign and_4_out = and_1_out & demultiplexer_1_out3;  // AND_Gate and_4, 16 bits wide
  assign and_5_out = or_1_out & demultiplexer_1_out4;  // AND_Gate and_5, 16 bits wide
  assign and_6_out = AddI_s & demultiplexer_1_out5;  // AND_Gate and_6, 16 bits wide
  assign and_7_out = shifter_1_out & demultiplexer_1_out6;  // AND_Gate and_7, 16 bits wide
  assign and_8_out = {{15{1'b0}}, comparator_1_lt[0]} & demultiplexer_1_out7;  // AND_Gate and_8, 16 bits wide
  assign and_9_out = divider_1_out & demultiplexer_1_out15;  // AND_Gate and_9, 16 bits wide
  assign and_10_out = {{15{1'b0}}, comparator_1_eq[0]} & demultiplexer_1_out12;  // AND_Gate and_10, 16 bits wide
  assign and_11_out = demultiplexer_1_out13 & or_3_out;  // AND_Gate and_11, 16 bits wide
  Multiplexer #(.width(16), .disabled(0)) multiplexer_1 (
    .in0(main_1_lo), .in1(main_1_hi), .out(multiplexer_1_out), .sel(demultiplexer_1_out8[0]), .en(or_4_out[0]));
  assign {or_4_out_2, or_4_out[0]} = {demultiplexer_1_out8_2, demultiplexer_1_out8[0]} | demultiplexer_1_out9;  // OR_Gate or_4, 16 bits wide
  assign R = and_2_out | and_3_out | multiplexer_1_out | and_4_out | and_5_out | and_6_out | and_7_out | and_8_out | and_10_out | and_11_out | and_9_out;  // OR_Gate or_5, 16 bits wide
endmodule
