// Logisim project ALUAdder.circ as structural Verilog: 1 circuit, main circuit main
module main (
  input  [15:0] A,
  input  C_in,
  input  [15:0] B,
  output [15:0] S,
  output C_out
);

  wire main_1_c_out, main_2_c_out, main_3_c_out, main_4_c_out, main_5_c_out, main_6_c_out, main_7_c_out,
       main_8_c_out, main_9_c_out, main_10_c_out, main_11_c_out, main_12_c_out, main_13_c_out, main_14_c_out,
       main_15_c_out;

  Adder_main main_1 (.A(A[0]), .B(B[0]), .C_in(C_in), .C_out(main_1_c_out), .Sum(S[0]));
  Adder_main main_2 (.A(A[1]), .B(B[1]), .C_in(main_1_c_out), .C_out(main_2_c_out), .Sum(S[1]));
  Adder_main main_3 (.A(A[2]), .B(B[2]), .C_in(main_2_c_out), .C_out(main_3_c_out), .Sum(S[2]));
  Adder_main main_4 (.A(A[3]), .B(B[3]), .C_in(main_3_c_out), .C_out(main_4_c_out), .Sum(S[3]));
  Adder_main main_5 (.A(A[4]), .B(B[4]), .C_in(main_4_c_out), .C_out(main_5_c_out), .Sum(S[4]));
  Adder_main main_6 (.A(A[5]), .B(B[5]), .C_in(main_5_c_out), .C_out(main_6_c_out), .Sum(S[5]));
  Adder_main main_7 (.A(A[6]), .B(B[6]), .C_in(main_6_c_out), .C_out(main_7_c_out), .Sum(S[6]));
  Adder_main main_8 (.A(A[7]), .B(B[7]), .C_in(main_7_c_out), .C_out(main_8_c_out), .Sum(S[7]));
  Adder_main main_9 (.A(A[8]), .B(B[8]), .C_in(main_8_c_out), .C_out(main_9_c_out), .Sum(S[8]));
  Adder_main main_10 (.A(A[9]), .B(B[9]), .C_in(main_9_c_out), .C_out(main_10_c_out), .Sum(S[9]));
  Adder_main main_11 (.A(A[10]), .B(B[10]), .C_in(main_10_c_out), .C_out(main_11_c_out), .Sum(S[10]));
  Adder_main main_12 (.A(A[11]), .B(B[11]), .C_in(main_11_c_out), .C_out(main_12_c_out), .Sum(S[11]));
  Adder_main main_13 (.A(A[12]), .B(B[12]), .C_in(main_12_c_out), .C_out(main_13_c_out), .Sum(S[12]));
  Adder_main main_14 (.A(A[13]), .B(B[13]), .C_in(main_13_c_out), .C_out(main_14_c_out), .Sum(S[13]));
  Adder_main main_15 (.A(A[14]), .B(B[14]), .C_in(main_14_c_out), .C_out(main_15_c_out), .Sum(S[14]));
  Adder_main main_16 (.A(A[15]), .B(B[15]), .C_in(main_15_c_out), .C_out(C_out), .Sum(S[15]));
endmodule
