// Logisim project ALUMult.circ as structural Verilog: 1 circuit, main circuit main
module main (
  input  [15:0] A,
  input  [15:0] B,
  input  write,
  input  clk,
  output [15:0] lo,
  output [15:0] hi
);

  wire [31:0] multiplier_1_out;

  Multiplier #(.width(32)) multiplier_1 (
    .a({{16{1'b0}}, A}), .b({{16{1'b0}}, B}), .out(multiplier_1_out), .cin({32{1'b0}}));  // open: cout
  Register #(.width(16), .trigger("falling")) register_1 (
    .D(multiplier_1_out[15:0]), .en(write), .Q(lo), .clk(clk));  // open: clr
  Register #(.width(16), .trigger("falling")) register_2 (
    .D(multiplier_1_out[31:16]), .en(write), .Q(hi), .clk(clk));  // open: clr
endmodule
