// Logisim project ControlUnit.circ as structural Verilog: 1 circuit, main circuit main
module main (
  input  [5:0] Opcode,
  input  clk,
  output Jump,
  output RegDst,
  output MemToReg,
  output MemWrite,
  output Branch,
  output RegWrite,
  output [1:0] ALUSrc
);

  wire demultiplexer_1_out0, demultiplexer_1_out1, demultiplexer_1_out3, demultiplexer_1_out4,
       demultiplexer_1_out5, demultiplexer_1_out7, demultiplexer_1_out8, demultiplexer_1_out9,
       demultiplexer_1_out12, demultiplexer_1_out15;
  wire [2:0] or_2_out;

  Demultiplexer #(.select(4), .disabled(0)) demultiplexer_1 (
    .out0(demultiplexer_1_out0), .out1(demultiplexer_1_out1), .out3(demultiplexer_1_out3),
    .out4(demultiplexer_1_out4), .out5(demultiplexer_1_out5), .out6(or_2_out[1]),
    .out7(demultiplexer_1_out7), .out8(demultiplexer_1_out8), .out9(demultiplexer_1_out9), .out10(MemToReg),
    .out11(MemWrite), .out12(demultiplexer_1_out12), .out13(or_2_out[2]), .out14(Jump),
    .out15(demultiplexer_1_out15), .in(1'b1), .sel(Opcode[3:0]), .en(clk));  // open: out2
  or or_1 (RegWrite, demultiplexer_1_out0, demultiplexer_1_out1, demultiplexer_1_out3, demultiplexer_1_out4, demultiplexer_1_out5, demultiplexer_1_out15, or_2_out[1], demultiplexer_1_out7, demultiplexer_1_out8, demultiplexer_1_out9, MemToReg);
  or or_2 (or_2_out[0], demultiplexer_1_out5, MemToReg, MemWrite);
  or or_3 (RegDst, demultiplexer_1_out5, MemToReg, MemWrite, demultiplexer_1_out12, or_2_out[2]);
  or or_4 (Branch, demultiplexer_1_out12, or_2_out[2]);
  Multiplexer #(.select(3), .width(2), .disabled(0), .enable("false")) multiplexer_1 (
    .in0(2'b00), .in1(2'b01), .in2(2'b10), .in4(2'b11), .out(ALUSrc), .sel(or_2_out));  // open: in3, in5, in6, in7
endmodule
