// Logisim project DataMemory.circ as structural Verilog: 1 circuit, main circuit main
module main (
  input  [15:0] Data_Address,
  input  [15:0] Write_Data,
  input  Write,
  input  clk,
  output [15:0] Load___Store_Data
);

  wire not_1_out, not_2_out;

  not not_1 (not_1_out, Write);
  not not_2 (not_2_out, clk);
  RAM #(.addrWidth(16), .dataWidth(16), .bus("separate")) ram_1 (
    .addr(Data_Address), .din(Write_Data), .data(Load___Store_Data), .str(Write), .sel(1'b1),
    .clk(not_2_out), .ld(not_1_out), .clr(1'b0));
endmodule
