// Logisim project InstructionMemory.circ as structural Verilog: 1 circuit, main circuit main
module main (
  input  [15:0] Instruction_Address,
  input  clk,
  output [31:0] Instruction
);

  RAM #(.addrWidth(16), .dataWidth(32)) ram_1 (
    .addr(Instruction_Address), .data(Instruction), .sel(1'b1), .clk(clk), .ld(1'b1), .clr(1'b0));
endmodule
