// Logisim project PC.circ as structural Verilog: 1 circuit, main circuit main
module main (
  input  [15:0] in,
  input  in_2,
  output [15:0] out
);

  Register #(.width(16), .trigger("falling")) register_1 (.D(in), .en(1'b1), .Q(out), .clk(in_2));  // open: clr
endmodule
