// Logisim project Single Cycle CPU [Main].circ as structural Verilog: 1 circuit, main circuit main
module main (
);

  wire clock_1_out, main_4_branch, main_4_memtoreg, main_4_memwrite, main_4_regdst, main_4_regwrite;
  wire [1:0] main_4_alusrc, main_4_jump;
  wire [4:0] multiplexer_1_out, rs, rt;
  wire [5:0] \function , opcode;
  wire [15:0] immediate_t, main_1_out, main_2_s, main_5_s, main_6_s, main_7_read_data_1, main_7_read_data_2,
       main_8_r, main_9_load___store_data, multiplexer_2_out, multiplexer_3_out, multiplexer_4_out;
  wire [15:5] undriven;
  wire [15:6] immediate;

  Clock clock_1 (.out(clock_1_out));
  PC_main main_1 (.in(multiplexer_2_out), .out(main_1_out), .in_2(clock_1_out));
  ALUAdder_main main_2 (.A(main_1_out), .C_in(1'b0), .B(16'h1), .S(main_2_s));  // open: C_out
  InstructionMemory_main main_3 (
    .Instruction_Address(main_1_out), .Instruction({opcode, rs, rt, immediate, \function }), .clk(clock_1_out));
  ControlUnit_main main_4 (
    .Jump(main_4_jump[0]), .RegDst(main_4_regdst), .MemToReg(main_4_memtoreg), .Opcode(opcode),
    .MemWrite(main_4_memwrite), .clk(clock_1_out), .Branch(main_4_branch), .RegWrite(main_4_regwrite),
    .ALUSrc(main_4_alusrc));
  Multiplexer #(.width(5)) multiplexer_1 (
    .in0(immediate[15:11]), .in1(rt), .out(multiplexer_1_out), .sel(main_4_regdst), .en(clock_1_out));
  ALUAdder_main main_5 (.A(immediate_t), .C_in(1'b0), .B(main_2_s), .S(main_5_s));  // open: C_out
  ALUAdder_main main_6 (.A({immediate, \function }), .C_in(1'b0), .B(main_2_s), .S(main_6_s));  // open: C_out
  Multiplexer #(.select(2), .width(16), .disabled(0)) multiplexer_2 (
    .in0(main_2_s), .in1(main_5_s), .in2(main_6_s), .out(multiplexer_2_out), .sel(main_4_jump),
    .en(clock_1_out));  // open: in3
  and and_1 (main_4_jump[1], main_4_branch, main_8_r[0]);
  RegisterFile_main main_7 (
    .RegWrite(main_4_regwrite), .rdAddr(multiplexer_1_out), .Data(multiplexer_4_out),
    .Read_Data_1(main_7_read_data_1), .Read_Data_2(main_7_read_data_2), .clk(clock_1_out), .rtAddr(rt),
    .rsAddr(rs));
  Multiplexer #(.select(2), .width(16)) multiplexer_3 (
    .in0(main_7_read_data_2), .in1(immediate_t), .in2({undriven, immediate[10:6]}), .in3({16{1'b0}}),
    .out(multiplexer_3_out), .sel(main_4_alusrc), .en(clock_1_out));
  ALU_main main_8 (.A(main_7_read_data_1), .B(multiplexer_3_out), .ALUOpcode(opcode), .R(main_8_r), .clk(clock_1_out));
  DataMemory_main main_9 (
    .Data_Address(main_8_r), .Load___Store_Data(main_9_load___store_data), .clk(clock_1_out),
    .Write(main_4_memwrite), .Write_Data(main_7_read_data_2));
  Multiplexer #(.width(16)) multiplexer_4 (
    .in0(main_8_r), .in1(main_9_load___store_data), .out(multiplexer_4_out), .sel(main_4_memtoreg),
    .en(clock_1_out));

  // Other names for the same wires on the sheet: shamt[4:0] = immediate[10:6];
  //   target_address[25:0] = {rs, rt, immediate, \function }; immediate[5:0] = \function ; rd[4:0] = immediate[15:11]

  // Notes on the sheet:
  //   Jump
  //   RegDst
  //   MemToReg
  //   MemWrite
  //   Branch
  //   RegWrite
  //   ALUSrc
endmodule
